# Fritzing sketch Fritzing Wiring Sketch (saved by Fritzing 0.9.3b)
circuit board: 8.46667cm x 5.64444cm
breadboards: 1

parts:
  Part1 = Arduino Nano (Rev3.0)
  S1 = Pushbutton [package="[THT]"]
  R1 = Resistor [tolerance=±5% resistance=220 package=THT]
  LED1 = LED - 5mm [color="Red (633nm)" package="5 mm [THT]"]
  R2 = Resistor [tolerance=±5% resistance=220 package=THT]
  R3 = Rotary Potentiometer (Small) [maximum_resistance=100kΩ package=THT]

nets:
  N1: Part1.GND, R1.Pin_0, LED1.cathode, R3.leg1
  N2: Part1.D2, Part1.5V, S1.Pin_1, S1.Pin_2, R3.leg2
  N3: Part1.D6, R2.Pin_1
  N4: Part1.A0, R3.wiper
  N5: S1.Pin_3, S1.Pin_4, R1.Pin_1
  N6: LED1.anode, R2.Pin_0
